# Fritzing sketch voletroulantbouton (saved by Fritzing 0.9.3b)
circuit board: 2.55331cm x 4.42447cm
breadboards: 2

parts:
  NodeMCU = NodeMCU V1.0
  R1 = Resistor [tolerance=±5% resistance=10k package=THT]
  R2 = Resistor [tolerance=±5% resistance=10k package=THT]
  ULN2803 = ULN2803A [package=THT]
  M2 = female pin header, 1 pin [form="♀ (female)"]
  M1 = female pin header, 1 pin [form="♀ (female)"]
  M3 = female pin header, 1 pin [form="♀ (female)"]
  M4 = female pin header, 1 pin [form="♀ (female)"]

nets:
  N1: NodeMCU.D1, R2.Pin_1
  N2: NodeMCU.D2, R1.Pin_1
  GND: NodeMCU.GND, R1.Pin_0, R2.Pin_0, ULN2803.0V
  N3: NodeMCU.D5, ULN2803.In_1
  N4: NodeMCU.D6, ULN2803.In_2
  N5: NodeMCU.D7, ULN2803.In_3
  N6: NodeMCU.D8, ULN2803.In_4
  5V: NodeMCU.Vin
  N7: ULN2803.Out_4, M4.pin1
  N8: ULN2803.Out_3, M3.pin1
  N9: ULN2803.Out_2, M2.pin1
  N10: ULN2803.Out_1, M1.pin1

notes:
  Vcc-ULN
  GND
  int-down
  int-up
  3V3

custom parts:
  NodeMCU V1.0: ESP8266 based NodeMCU
